# Fritzing sketch Untitled Sketch (saved by Fritzing 0.8.7b)
breadboards: 1

parts:
  R1 = Resistor [tolerance=±5% resistance=100 package="0805 [SMD]"]  # not connected
  R2 = Resistor [tolerance=±5% resistance=100 package="0805 [SMD]"]  # not connected
  Eleman1 = Arduino Uno (Rev3)
  LED1 = RGB LED (com. anode, rbg) [package="5 mm [THT]"]
  J1 = Piezo Speaker
  LED2 = RGB LED (com. anode, rbg) [package="5 mm [THT]"]

nets:
  N1: Eleman1.A0, LED2.red_cathode
  N2: Eleman1.D4, J1.pin2
  N3: Eleman1.5V, LED1.blue_cathode, LED2.blue_cathode
  N4: Eleman1.GND, LED2.common_anode

notes:
  manyetik sensor kimi goturek
